# Fritzing sketch PCB[FritzingSketch] (saved by Fritzing 0.9.3b)
circuit board: 6.88566cm x 5.36311cm
breadboards: 1

parts:
  Part1 = Arduino Uno (Rev3) - ICSP
  Instrument_Trigger = SWITCH-MOMENTARY-2 [package=tactile-pth-12mm]
  Clock = thonkiconn [package="PG203J [THT]"]
  Write = thonkiconn [package="PG203J [THT]"]
  StartStop = thonkiconn [package="PG203J [THT]"]
  MIDI_In = MIDI_CONN_FEMALE [package=din_5_female]
  D1 = Rectifier Diode [part_number=1N4001 package="300 mil [THT]"]
  R1 = Resistor [tolerance=±5% resistance=220 package=THT]
  R2 = Resistor [tolerance=±5% resistance=10k package=THT]
  6N138 = IC, DIP package, 8 pins [chip_label=IC]

nets:
  N1: Part1.D0/RX, R2.Pin_1, 6N138.pin6
  N2: Part1.D2, Instrument_Trigger.1
  N3: Part1.D3_PWM, Clock.signal
  N4: Part1.D4, Write.signal
  N5: Part1.D5_PWM, StartStop.signal
  N6: Part1.5V, R2.Pin_0, 6N138.pin8
  N7: Part1.GND, Instrument_Trigger.2, Clock.switch, Clock.ground, Write.ground, StartStop.ground, 6N138.pin5
  N8: MIDI_In.MIDI_IN, D1.anode, 6N138.pin3
  N9: MIDI_In.MIDI_OUT, R1.Pin_0
  N10: D1.cathode, R1.Pin_1, 6N138.pin2

notes:
  Compusync 78

custom parts:
  thonkiconn: mono switched Jack 3.5mm
